# Fritzing sketch velocista (saved by Fritzing 0.9.1b)

parts:
  Parte1 = Motor Driver 1A Dual TB6612FNG
  Parte2 = Arduino Nano (Rev3.0)
  BAT2 = Battery Holders [package=lipo-1100mAh]
  M1 = DC Motor
  M2 = DC Motor
  S1 = Pololu QTR-8 Reflectabce Sensor array [package=THT]

nets:
  N1: Parte1.B01, M1.pin_1
  N2: Parte1.B02, M1.pin_2
  N3: Parte1.A02, M2.pin_2
  N4: Parte1.A01, M2.pin_1
  VCC: Parte1.VCC, Parte2.5V, S1.pin14, S1.pin22
  N5: Parte1.PWMA, Parte2.D3
  N6: Parte1.PWMB, Parte2.D5
  N7: Parte2.D2, S1.pin12
  N8: Parte2.D4, S1.pin11
  N9: Parte2.D6, S1.pin10
  N10: Parte2.D7, S1.pin9
  N11: Parte2.D8, S1.pin8
  N12: Parte2.D9, S1.pin7
  N13: Parte2.D10, S1.pin6
  N14: Parte2.D11/MOSI, S1.pin5
  N15: Parte2.D12/MISO, S1.pin13
  N16: Parte2.VIN, BAT2.+
  N17: Parte2.GND, BAT2.-
